# Fritzing sketch rfid (saved by Fritzing 0.9.3b)
breadboards: 1

parts:
  Part1 = Arduino Uno (Rev3) - ICSP
  J1 = Piezo Speaker
  IC1 = DS3231MZ Real Time Clock
  J2 = Basic Servo
  LCD2 = LCD screen
  LCM1602_IIC2 = LCM1602 IIC [part_number="LCM1602 IIC" chip_label="LCM1602 IIC" package="DIP (Dual Inline) [THT]"]
  Part3 = RFID-RC522-v2

nets:
  N1: Part1.A4/SDA, IC1.Pin_7, LCM1602_IIC2.SDA
  N2: Part1.A5/SCL, IC1.Pin_8, LCM1602_IIC2.SCL
  N3: Part1.ICSP_MOSI, Part1.D11_PWM/MOSI, Part3.MOSI
  N4: Part1.D8, J1.pin2
  N5: Part1.D9_PWM, Part3.RST
  N6: Part1.D10_PWM/SS, Part3.SDA
  N7: Part1.D12/MISO, Part3.MISO
  N8: Part1.D13/SCK, Part3.SCK
  GND: Part1.GND, J1.pin1, IC1.Pin_5, J2.gnd, LCM1602_IIC2.GND, Part3.GND
  N9: Part1.D6_PWM, J2.pulse
  N10: Part1.3V3, Part3.3_3V
  5V: Part1.5V, IC1.Pin_2, LCM1602_IIC2.VCC
  VSS: LCD2.VSS, LCM1602_IIC2.VSS
  VDD: LCD2.VDD, LCM1602_IIC2.VDD
  N11: LCD2.V0, LCM1602_IIC2.V0
  N12: LCD2.RS, LCM1602_IIC2.RS
  N13: LCD2.R/W, LCM1602_IIC2.RW
  N14: LCD2.E, LCM1602_IIC2.E
  N15: LCD2.DB0, LCM1602_IIC2.D0
  N16: LCD2.DB1, LCM1602_IIC2.D1
  N17: LCD2.DB2, LCM1602_IIC2.D2
  N18: LCD2.DB3, LCM1602_IIC2.D3
  N19: LCD2.DB4, LCM1602_IIC2.D4
  N20: LCD2.DB5, LCM1602_IIC2.D5
  N21: LCD2.DB6, LCM1602_IIC2.D6
  N22: LCD2.DB7, LCM1602_IIC2.D7
  N23: LCD2.LED+, LCM1602_IIC2.A
  N24: LCD2.LED-, LCM1602_IIC2.K

custom parts:
  DS3231MZ Real Time Clock: DS3231MZ Real Time Clock. SO-8 surface mount version.
  LCM1602 IIC: I2C-Module to use a 1602 or 2004 LCD on with the wire.h libory Serial LCD Modul
  RFID-RC522-v2: A simple China made RFID-RC522 Reader; do check the pin labels, as this is a MFRC522 based clone.
